// Digital circuit hazard_unit.dig as structural Verilog
module hazard_unit (
  input  [4:0] RR0_2,
  input  [4:0] RR1_2,
  input  [4:0] WR_4,
  input  [4:0] WR_3,
  input  RFW_4,
  input  RFW_3,
  input  CLR,
  input  PCbr2,
  input  MR_3,
  output [1:0] FRD_0_Sel,
  output [1:0] FRD_1_Sel,
  output FLUSH_IF,
  output FLUSH_DR,
  output FLUSH_EX,
  output STALL_DR,
  output STALL_IF,
  output STALL_EX
);

  wire and_1_out, and_2_out, and_3_out, and_4_out, comparator_1_eq, comparator_2_eq, comparator_3_eq,
       comparator_4_eq, comparator_5_eq;

  Comparator #(.Bits(5)) comparator_1 (.a(RR0_2), .b(WR_4), .eq(comparator_1_eq));  // open: gt, lt
  Comparator #(.Bits(5)) comparator_2 (.a(RR0_2), .b(WR_3), .eq(comparator_2_eq));  // open: gt, lt
  Comparator #(.Bits(5)) comparator_3 (.a(RR1_2), .b(WR_4), .eq(comparator_3_eq));  // open: gt, lt
  Comparator #(.Bits(5)) comparator_4 (.a(RR1_2), .b(WR_3), .eq(comparator_4_eq));  // open: gt, lt
  and and_1 (and_1_out, comparator_1_eq, RFW_4);
  and and_2 (and_2_out, comparator_2_eq, RFW_3);
  and and_3 (and_3_out, comparator_3_eq, RFW_4);
  and and_4 (and_4_out, comparator_4_eq, RFW_3);
  or or_1 (FLUSH_DR, CLR, PCbr2);
  Comparator #(.Bits(5)) comparator_5 (.a(RR0_2), .b(WR_3), .eq(comparator_5_eq));  // open: gt, lt
  PriorityEncoder #(.Selector_Bits(2)) priorityencoder_1 (
    .in0(1'b1), .in1(and_2_out), .in2(and_1_out), .in3(1'b0), .num(FRD_0_Sel));  // open: any
  PriorityEncoder #(.Selector_Bits(2)) priorityencoder_2 (
    .in0(1'b1), .in1(and_4_out), .in2(and_3_out), .in3(1'b0), .num(FRD_1_Sel));  // open: any
  and and_5 (FLUSH_EX, comparator_5_eq, FLUSH_DR, MR_3);
  not not_1 (STALL_IF, FLUSH_EX);
  not not_2 (STALL_DR, FLUSH_EX);
  not not_3 (STALL_EX, FLUSH_EX);

  assign FLUSH_IF = FLUSH_DR;
endmodule
